// Logisim project PS2Keyboard.circ as structural Verilog: 1 circuit, main circuit main
module main (
  input  [7:0] in_1
);

  wire and_1_out, and_2_out, and_3_out, and_4_out, button_1_out, button_2_out, button_3_out, d_ff_1_q,
       DATA_LINE, nand_1_out, nand_2_out, nor_1_out, nor_2_out, not_3_out, not_4_out, not_6_out, PS2_CLK,
       PS2_DATA, pull_resistor_1_node, pull_resistor_2_node, pull_resistor_4_node, pull_resistor_5_node, S1,
       S11, s_r_ff_1_q, SHIFT, SYS_CLK;
  wire [3:0] counter_1_q, not_5_out;

  Button button_1 (.out(button_1_out));
  Button button_2 (.out(button_2_out));
  _74161 #(.ShowInternalStructure("true")) u_74161_1 ();  // open: pin1, pin2, pin3, pin4, pin5, pin6, pin7, pin15, pin14, pin13, pin12, pin11, pin10, pin9
  nor nor_1 (nor_1_out, button_1_out, nor_2_out);
  // NOT_Gate not_1 has open pins: in=nor_1_out, out=open
  nor nor_2 (nor_2_out, nor_1_out, button_2_out);
  // NOT_Gate not_2 has open pins: in=nor_2_out, out=open
  Button button_3 (.out(button_3_out));
  Clock clock_1 (.out(SYS_CLK));
  // Digital_Oscilloscope #(.nState(16)) digital_oscilloscope_1: pin names not known; wires that end beside it: SYS_CLK, PS2_CLK, S1, S11, SHIFT, DATA_LINE, PS2_DATA
  D_Flip_Flop d_ff_1 (
    .D(pull_resistor_1_node), .clk(button_3_out), .Q(d_ff_1_q), .reset(and_1_out));  // open: Qn, preset
  Pull_Resistor #(.pull(1)) pull_resistor_1 (.node(pull_resistor_1_node));
  and and_1 (and_1_out, d_ff_1_q, S1);
  S_R_Flip_Flop #(.trigger("high")) s_r_ff_1 (
    .S(d_ff_1_q), .R(S11), .clk(pull_resistor_2_node), .Q(s_r_ff_1_q));  // open: reset, Qn, preset
  Pull_Resistor #(.pull(1)) pull_resistor_2 (.node(pull_resistor_2_node));
  not not_3 (not_3_out, S1);
  Pull_Resistor #(.pull(1)) pull_resistor_3 (.node(PS2_CLK));
  Transistor #(.\type ("n")) transistor_1 (.in(1'b0), .out(PS2_CLK), .gate(and_2_out));
  not not_4 (not_4_out, and_2_out);
  and and_2 (and_2_out, s_r_ff_1_q, SYS_CLK);
  and and_3 (and_3_out, not_3_out, SHIFT);
  Counter #(.max('hf), .width(4)) counter_1 (
    .clr(S11), .load(pull_resistor_4_node), .up(pull_resistor_5_node), .count(s_r_ff_1_q), .clk(not_4_out),
    .Q(counter_1_q));  // open: D, carry
  Pull_Resistor pull_resistor_4 (.node(pull_resistor_4_node));
  Pull_Resistor #(.pull(1)) pull_resistor_5 (.node(pull_resistor_5_node));
  // Shift_Register shift_register_1: pin names not known; wires that end beside it: S11, S1, and_3_out, SYS_CLK, DATA_LINE
  Pull_Resistor pull_resistor_6 ();  // open: node
  assign not_5_out = ~counter_1_q;  // NOT_Gate not_5, 4 bits wide
  not not_6 (not_6_out, DATA_LINE);
  not not_7 (S1, nand_1_out);
  nand nand_1 (nand_1_out, counter_1_q[0], not_5_out[1], not_5_out[2], not_5_out[3]);
  not not_8 (S11, nand_2_out);
  nand nand_2 (nand_2_out, counter_1_q[0], counter_1_q[1], counter_1_q[3], not_5_out[2]);
  nand nand_3 (SHIFT, not_5_out[0], not_5_out[1], not_5_out[2], not_5_out[3]);
  Pull_Resistor #(.pull(1)) pull_resistor_7 (.node(PS2_DATA));
  Transistor #(.\type ("n")) transistor_2 (.in(1'b0), .out(PS2_DATA), .gate(and_4_out));
  and and_4 (and_4_out, not_6_out, SHIFT);

  // Other names for the same wires on the sheet: KEYCODE[7:0] = in_1
endmodule
